# Fritzing sketch BOTAO-SERIAL (saved by Fritzing 1.0.4)
breadboards: 2

parts:
  Componente5 = Arduino Uno (Rev3)
  HC-SR04_Sensor_3 = HC-SR04 Ultrasonic Distance Sensor
  NEOPIXEL2 = Neopixel Strip -- White (60/m)
  VCC2 = 4 x AAA Battery Mount [internal_resistance=0.1Ω]
  J4 = Piezo Speaker
  Componente7 = Arduino Uno (Rev3)
  LED4 = LED - 3mm [color="Red (635nm)" current=0.030A package="3 mm [THT]"]
  LED5 = LED - 3mm [color="Blue (430nm)" current=0.030A package="3 mm [THT]"]
  LED6 = LED - 3mm [color="Red (635nm)" current=0.030A package="3 mm [THT]"]
  LED7 = LED - 3mm [color="Blue (430nm)" current=0.030A package="3 mm [THT]"]
  S6 = Toggle Switch spst [package=THT]

nets:
  GND: Componente5.GND, HC-SR04_Sensor_3.GND, NEOPIXEL2.GND, VCC2.-, J4.pin1, Componente7.GND, LED4.cathode, LED5.cathode, LED6.cathode, LED7.cathode
  N1: Componente5.D4, Componente7.D5_PWM
  N2: Componente5.D5_PWM, NEOPIXEL2.+5V
  N3: Componente5.D6_PWM, HC-SR04_Sensor_3.TRIG
  N4: Componente5.D7, HC-SR04_Sensor_3.ECHO
  5V: Componente5.5V, HC-SR04_Sensor_3.VCC, NEOPIXEL2.DI
  VIN: Componente5.VIN, Componente7.VIN, S6.COM
  N5: VCC2.+, S6.L1
  N6: J4.pin2, Componente7.D7
  N7: Componente7.D8, LED6.anode
  N8: Componente7.D9_PWM, LED7.anode
  N9: Componente7.D12/MISO, LED5.anode
  N10: Componente7.D13/SCK, LED4.anode

custom parts:
  Neopixel Strip -- White (60/m): Neopixel Strip, White, 60 pixels per meter.
  Toggle Switch spst: Toggle Switch single pole single throw
