# Fritzing sketch PORTAL-SLAVE (saved by Fritzing 1.0.4)
breadboards: 1

parts:
  Componente5 = Arduino Uno (Rev3)
  Componente6 = Bluetooth HC-05 Macho
  R5 = Photocell (LDR) [power=0.25W dark_resistance_@0.01lx=300kΩ light_resistance_@100lx=400Ω luminance=10lx package=THT]
  R6 = Resistor [tolerance=±5% power=0.25W resistance=220 package=THT]
  NEOPIXEL2 = Neopixel Strip -- White (60/m)
  J3 = Basic Servo
  S5 = Toggle Switch spst [package=THT]
  VCC2 = 4 x AAA Battery Mount [internal_resistance=0.1Ω]

nets:
  N1: Componente5.A0, R5.pin_1, R6.Pin_0
  N2: Componente5.D8, J3.pulse
  N3: Componente5.D12/MISO, NEOPIXEL2.+5V
  N4: Componente5.D2, Componente6.TXD
  N5: Componente5.D3_PWM, Componente6.RXD
  5V: Componente5.5V, Componente6.VCC, R5.pin_0, NEOPIXEL2.DI
  GND: Componente5.GND, Componente6.GND, R6.Pin_1, NEOPIXEL2.GND, J3.gnd, S5.COM
  N6: Componente5.VIN, VCC2.+
  N7: S5.L1, VCC2.-

custom parts:
  Neopixel Strip -- White (60/m): Neopixel Strip, White, 60 pixels per meter.
  Toggle Switch spst: Toggle Switch single pole single throw
