# Fritzing sketch PORTAR-MASTER (saved by Fritzing 1.0.4)
breadboards: 1

parts:
  NEOPIXEL1 = Neopixel Strip -- White (60/m)
  Componente3 = Arduino Uno (Rev3)
  Componente4 = Bluetooth HC-05 Macho
  R3 = Photocell (LDR) [power=0.25W dark_resistance_@0.01lx=300kΩ light_resistance_@100lx=400Ω luminance=10lx package=THT]
  R4 = Resistor [tolerance=±5% power=0.25W resistance=220 package=THT]
  HC-SR04_Sensor_2 = HC-SR04 Ultrasonic Distance Sensor
  LED2 = LED - 3mm [color="Blue (430nm)" current=0.030A package="3 mm [THT]"]
  J2 = Basic Servo
  S2 = H-Bridge with L298N
  S3 = Toggle Switch spst [package=THT]
  VCC1 = 4 x AAA Battery Mount [internal_resistance=0.1Ω]

nets:
  N1: NEOPIXEL1.+5V, Componente3.D12/MISO
  VCC: NEOPIXEL1.DI, Componente3.5V, Componente4.VCC, R3.pin_0, HC-SR04_Sensor_2.VCC, J2.vcc
  GND: NEOPIXEL1.GND, Componente3.GND, Componente4.GND, R4.Pin_1, HC-SR04_Sensor_2.GND, LED2.cathode, J2.gnd, S2.GND, S3.COM
  N2: Componente3.A0, R3.pin_1, R4.Pin_0
  N3: Componente3.D8, HC-SR04_Sensor_2.TRIG
  N4: Componente3.D9_PWM, HC-SR04_Sensor_2.ECHO
  N5: Componente3.D10_PWM/SS, S2.IN2
  N6: Componente3.D11_PWM/MOSI, S2.IN1
  N7: Componente3.D2, Componente4.TXD
  N8: Componente3.D3_PWM, Componente4.RXD
  N9: Componente3.D4, LED2.anode
  N10: Componente3.D5_PWM, Componente4.State
  N11: Componente3.D6_PWM, J2.pulse
  N12: S2.12V, VCC1.+
  N13: S3.L1, VCC1.-

notes:
  Conexão com o motor ev3
  Branco +
  Preto -

custom parts:
  Neopixel Strip -- White (60/m): Neopixel Strip, White, 60 pixels per meter.
  H-Bridge with L298N: h-bridge
  Toggle Switch spst: Toggle Switch single pole single throw
