# Fritzing sketch PORTAL-GUN (saved by Fritzing 1.0.4)
breadboards: 1

parts:
  Componente5 = Arduino Uno (Rev3)
  HC-SR04_Sensor_3 = HC-SR04 Ultrasonic Distance Sensor
  LED3 = LED - 3mm [color="Blue (430nm)" current=0.030A package="3 mm [THT]"]
  S5 = Toggle Switch spst [package=THT]
  VCC2 = 4 x AAA Battery Mount [internal_resistance=0.1Ω]
  LED5 = LED - 3mm [color="Blue (430nm)" current=0.030A package="3 mm [THT]"]
  LED6 = LED - 5mm [color="White (4500K)" current=0.030A package="5 mm [THT]"]

nets:
  N1: Componente5.D2, LED6.anode
  N2: Componente5.D3_PWM, LED5.anode
  N3: Componente5.D4, LED3.anode
  N4: Componente5.D5_PWM, HC-SR04_Sensor_3.TRIG
  N5: Componente5.D6_PWM, HC-SR04_Sensor_3.ECHO
  5V: Componente5.5V, HC-SR04_Sensor_3.VCC
  GND: Componente5.GND, HC-SR04_Sensor_3.GND, LED3.cathode, S5.COM, LED5.cathode, LED6.cathode
  N6: S5.L1, VCC2.-

custom parts:
  Toggle Switch spst: Toggle Switch single pole single throw
